# Fritzing sketch basic_schematic (saved by Fritzing 0.9.3b)
breadboards: 1

parts:
  Y1 = CRYSTAL [package=tc26h]  # not connected
  C1 = Capacitor [part_number=22pF package=cap-pth-small2]
  C2 = Capacitor [part_number=22pF package=cap-pth-small2]
  Pro_Mini_3_3v_8MHz = Arduino Pro Mini (3.3V)
  U1 = 2.5mm Audio Jack [part_number=Audio package=stereojack2.5mm_smd]  # not connected

nets:
  GND: C1.1, C2.1, Pro_Mini_3_3v_8MHz.GND
  3.3V: Pro_Mini_3_3v_8MHz.VCC
  RESET: Pro_Mini_3_3v_8MHz.RESET

notes:
  SDA / SDIO
  SCL / SCLK
